// Logisim project alu.circ as structural Verilog: 1 circuit, main circuit alu
module alu (
  input  [31:0] A,
  input  [31:0] B,
  input  [3:0] ALUSel,
  output [31:0] Result
);

  wire comparator_1_lt;
  wire [31:0] add0, and1, mul10, mulh14, mulhu11, multiplier_2_out, multiplier_3_out, or2, sll6, slt7, sra5,
       srl4, sub12, xor3;
  wire [63:0] bit_extender_2_out, bit_extender_3_out, bit_extender_4_out, bit_extender_5_out;

  Comparator #(.width(32)) comparator_1 (.a(A), .b(B), .lt(comparator_1_lt));  // open: gt, eq
  Adder #(.width(32)) adder_1 (.a(A), .b(B), .out(add0));  // open: cin, cout
  assign and1 = A & B;  // AND_Gate and_1, 32 bits wide
  assign or2 = A | B;  // OR_Gate or_1, 32 bits wide
  assign xor3 = A ^ B;  // XOR_Gate xor_1, 32 bits wide
  Shifter #(.shift("lr"), .width(32)) shifter_1 (.in(A), .\dist (B[4:0]), .out(srl4));
  Shifter #(.shift("ar"), .width(32)) shifter_2 (.in(A), .\dist (B[4:0]), .out(sra5));
  Shifter #(.width(32)) shifter_3 (.in(A), .\dist (B[4:0]), .out(sll6));
  assign slt7 = {{31{1'b0}}, comparator_1_lt};  // Bit_Extender bit_extender_1
  assign bit_extender_2_out = {{32{A[31]}}, A};  // Bit_Extender bit_extender_2
  assign bit_extender_3_out = {{32{B[31]}}, B};  // Bit_Extender bit_extender_3
  assign bit_extender_4_out = {{32{1'b0}}, A};  // Bit_Extender bit_extender_4
  assign bit_extender_5_out = {{32{1'b0}}, B};  // Bit_Extender bit_extender_5
  Multiplier #(.mode("twosComplement"), .width(32)) multiplier_1 (.a(A), .b(B), .out(mul10));  // open: cin, cout
  Multiplier #(.mode("twosComplement"), .width(64)) multiplier_2 (
    .a(bit_extender_2_out), .b(bit_extender_3_out), .out({mulh14, multiplier_2_out}));  // open: cin, cout
  Subtractor #(.width(32)) subtractor_1 (.a(A), .b(B), .out(sub12));  // open: bin, bout
  Multiplier #(.width(64)) multiplier_3 (
    .a(bit_extender_4_out), .b(bit_extender_5_out), .out({mulhu11, multiplier_3_out}));  // open: cin, cout
  Multiplexer #(.enable("false"), .select(4), .width(32)) multiplexer_1 (
    .in0(add0), .in1(and1), .in2(or2), .in3(xor3), .in4(srl4), .in5(sra5), .in6(sll6), .in7(slt7),
    .in8({32{1'b0}}), .in9({32{1'b0}}), .in10(mul10), .in11(mulhu11), .in12(sub12), .in13(B), .in14(mulh14),
    .in15({32{1'b0}}), .out(Result), .sel(ALUSel));

  // Other names for the same wires on the sheet: bsel13[31:0] = B

  // Notes on the sheet:
  //   INPUTS to your circuit
  //   DON'T CHANGE THE LOCATIONS OF THE INPUTS AND OUTPUTS!
  //   OUTPUT from your circuit
endmodule
