// Logisim project cpu.circ as structural Verilog: 1 circuit, main circuit cpu
module cpu (
  input  clk,
  input  [31:0] INSTRUCTION,
  input  [31:0] READ_DATA,
  output [31:0] WRITE_ADDRESS,
  output [31:0] PROGRAM_COUNTER,
  output [31:0] ra,
  output [31:0] sp,
  output [31:0] t0,
  output [31:0] t1,
  output [31:0] t2,
  output [31:0] s0,
  output [31:0] s1,
  output [31:0] a0,
  output [31:0] tohost,
  output [3:0] WRITE_ENABLE,
  output [31:0] WRITE_DATA
);

  wire BSel, RegWEn;
  wire [3:0] ALUSel;
  wire [31:0] adder_1_out, alu_out, imm_out, INSTRUCTION_P, multiplexer_1_out, rd_1, rd_2;

  Register #(.width(32)) register_1 (.D(INSTRUCTION), .en(1'b1), .clk(clk), .Q(INSTRUCTION_P));  // open: clr
  Adder #(.width(32)) adder_1 (.a(PROGRAM_COUNTER), .b(32'h4), .out(adder_1_out));  // open: cin, cout
  Register #(.width(32)) PC (.D(adder_1_out), .en(1'b1), .clk(clk), .Q(PROGRAM_COUNTER));  // open: clr
  control_logic control_logic_1 (
    .RegWEn(RegWEn), .BSel(BSel), .ALUSel(ALUSel));  // open: CSRWen, PCSel, ImmSel, BrUn, ASel, MemRW, WBSel, CSRSel, inst, BrEq, BrLt
  imm_gen imm_gen_1 (.inst(INSTRUCTION_P), .imm(imm_out));  // open: ImmSel
  regfile regfile_1 (
    .rs1(INSTRUCTION_P[19:15]), .rs2(INSTRUCTION_P[24:20]), .rd(INSTRUCTION_P[11:7]), .Write_Data(alu_out),
    .RegWEn(RegWEn), .clk(clk), .ra(ra), .sp(sp), .t0(t0), .t1(t1), .t2(t2), .s0(s0), .s1(s1), .a0(a0),
    .Read_Data_1(rd_1), .Read_Data_2(rd_2));
  // branch_comp branch_comp_1: pin names not known
  Multiplexer #(.enable("false"), .width(32)) multiplexer_1 (
    .in0(rd_2), .in1(imm_out), .out(multiplexer_1_out), .sel(BSel));
  alu alu_1 (.Result(alu_out), .A(rd_1), .B(multiplexer_1_out), .ALUSel(ALUSel));
  // csr csr_1: pin names not known; wires that end beside it: tohost

  // Notes on the sheet:
  //   Output to IMEM
  //   IMEM (do **NOT** move this)
  //   Inputs from IMEM
  //   It is OK to move the PC, RegFile, ALU, MEM, Branch Comp, Imm Gen, and Control Logic to wherever is most convenient for you when constructing your CPU, and to delete this text
  //   Inputs/Outputs for testing. Do **NOT** move these.
  //   Outputs To DMEM
  //   DMEM (do **NOT** move this)
  //   Inputs From DMEM
endmodule
