// Logisim project imm_gen.circ as structural Verilog: 1 circuit, main circuit imm_gen
module imm_gen (
  input  [31:0] inst,
  input  [2:0] ImmSel,
  output [31:0] imm
);

  wire [31:0] ii, sbi, si, uji;

  Multiplexer #(.enable("false"), .select(3), .width(32)) multiplexer_1 (.sel(ImmSel));  // open: in0, in1, in2, in3, in4, in5, in6, in7, out
  assign ii = {{20{inst[31]}}, inst[31:20]};  // Bit_Extender bit_extender_1
  assign si = {{20{inst[31]}}, {inst[31:25], inst[11:7]}};  // Bit_Extender bit_extender_2
  assign sbi = {{19{inst[31]}}, {inst[31], inst[7], inst[30:25], inst[11:8], 1'b0}};  // Bit_Extender bit_extender_3
  assign imm = {{20{inst[31]}}, inst[31:20]};  // Bit_Extender bit_extender_4
  assign uji = {{11{inst[31]}}, {inst[31], inst[19:12], inst[20], inst[30:21], 1'b0}};  // Bit_Extender bit_extender_5

  // Other names for the same wires on the sheet: i8_11[3:0] = inst[11:8]; i7 = inst[7]; i20_30[10:0] = inst[30:20];
  //   i21_24[3:0] = inst[24:21]; ui[31:12] = inst[31:12]; i25_30[5:0] = inst[30:25]; i20 = inst[20];
  //   i12_19[7:0] = inst[19:12]; i31 = inst[31]

  // Notes on the sheet:
  //   INPUTS to your circuit
  //   DON'T CHANGE THE LOCATIONS OF THE INPUTS AND OUTPUTS!
  //   OUTPUT from your circuit
endmodule
