// Logisim project regfile.circ as structural Verilog: 1 circuit, main circuit regfile
module regfile (
  input  [4:0] rs1,
  input  [4:0] rs2,
  input  [4:0] rd,
  input  [31:0] Write_Data,
  input  RegWEn,
  input  clk,
  output [31:0] ra,
  output [31:0] sp,
  output [31:0] t0,
  output [31:0] t1,
  output [31:0] t2,
  output [31:0] s0,
  output [31:0] s1,
  output [31:0] a0,
  output [31:0] Read_Data_1,
  output [31:0] Read_Data_2
);

  wire x1_we, x2_we, x3_we, x4_we, x5_we, x6_we, x7_we, x8_we, x9_we, x10_we, x11_we, x12_we, x13_we, x14_we,
       x15_we, x16_we, x17_we, x18_we, x19_we, x20_we, x21_we, x22_we, x23_we, x24_we, x25_we, x26_we,
       x27_we, x28_we, x29_we, x30_we, x31_we;
  wire [31:0] x0, x3_out, x4_out, x11_out, x12_out, x13_out, x14_out, x15_out, x16_out, x17_out, x18_out,
       x19_out, x20_out, x21_out, x22_out, x23_out, x24_out, x25_out, x26_out, x27_out, x28_out, x29_out,
       x30_out, x31_out;

  Register #(.width(32)) register_1 (.en(1'b0), .clk(clk), .Q(x0));  // open: D, clr
  Register #(.width(32)) register_2 (.D(Write_Data), .en(x4_we), .clk(clk), .Q(x4_out));  // open: clr
  Register #(.width(32)) register_3 (.D(Write_Data), .en(x8_we), .clk(clk), .Q(s0));  // open: clr
  Register #(.width(32)) register_4 (.D(Write_Data), .en(x12_we), .clk(clk), .Q(x12_out));  // open: clr
  Register #(.width(32)) register_5 (.D(Write_Data), .en(x16_we), .clk(clk), .Q(x16_out));  // open: clr
  Register #(.width(32)) register_6 (.D(Write_Data), .en(x20_we), .clk(clk), .Q(x20_out));  // open: clr
  Register #(.width(32)) register_7 (.D(Write_Data), .en(x24_we), .clk(clk), .Q(x24_out));  // open: clr
  Register #(.width(32)) register_8 (.D(Write_Data), .en(x28_we), .clk(clk), .Q(x28_out));  // open: clr
  Register #(.width(32)) register_9 (.D(Write_Data), .en(x1_we), .clk(clk), .Q(ra));  // open: clr
  Register #(.width(32)) register_10 (.D(Write_Data), .en(x5_we), .clk(clk), .Q(t0));  // open: clr
  Register #(.width(32)) register_11 (.D(Write_Data), .en(x9_we), .clk(clk), .Q(s1));  // open: clr
  Register #(.width(32)) register_12 (.D(Write_Data), .en(x13_we), .clk(clk), .Q(x13_out));  // open: clr
  Register #(.width(32)) register_13 (.D(Write_Data), .en(x17_we), .clk(clk), .Q(x17_out));  // open: clr
  Register #(.width(32)) register_14 (.D(Write_Data), .en(x21_we), .clk(clk), .Q(x21_out));  // open: clr
  Register #(.width(32)) register_15 (.D(Write_Data), .en(x25_we), .clk(clk), .Q(x25_out));  // open: clr
  Register #(.width(32)) register_16 (.D(Write_Data), .en(x29_we), .clk(clk), .Q(x29_out));  // open: clr
  Register #(.width(32)) register_17 (.D(Write_Data), .en(x2_we), .clk(clk), .Q(sp));  // open: clr
  Register #(.width(32)) register_18 (.D(Write_Data), .en(x6_we), .clk(clk), .Q(t1));  // open: clr
  Register #(.width(32)) register_19 (.D(Write_Data), .en(x10_we), .clk(clk), .Q(a0));  // open: clr
  Register #(.width(32)) register_20 (.D(Write_Data), .en(x14_we), .clk(clk), .Q(x14_out));  // open: clr
  Register #(.width(32)) register_21 (.D(Write_Data), .en(x18_we), .clk(clk), .Q(x18_out));  // open: clr
  Register #(.width(32)) register_22 (.D(Write_Data), .en(x22_we), .clk(clk), .Q(x22_out));  // open: clr
  Register #(.width(32)) register_23 (.D(Write_Data), .en(x26_we), .clk(clk), .Q(x26_out));  // open: clr
  Register #(.width(32)) register_24 (.D(Write_Data), .en(x30_we), .clk(clk), .Q(x30_out));  // open: clr
  Register #(.width(32)) register_25 (.D(Write_Data), .en(x3_we), .clk(clk), .Q(x3_out));  // open: clr
  Register #(.width(32)) register_26 (.D(Write_Data), .en(x7_we), .clk(clk), .Q(t2));  // open: clr
  Register #(.width(32)) register_27 (.D(Write_Data), .en(x11_we), .clk(clk), .Q(x11_out));  // open: clr
  Register #(.width(32)) register_28 (.D(Write_Data), .en(x15_we), .clk(clk), .Q(x15_out));  // open: clr
  Register #(.width(32)) register_29 (.D(Write_Data), .en(x19_we), .clk(clk), .Q(x19_out));  // open: clr
  Register #(.width(32)) register_30 (.D(Write_Data), .en(x23_we), .clk(clk), .Q(x23_out));  // open: clr
  Register #(.width(32)) register_31 (.D(Write_Data), .en(x27_we), .clk(clk), .Q(x27_out));  // open: clr
  Register #(.width(32)) register_32 (.D(Write_Data), .en(x31_we), .clk(clk), .Q(x31_out));  // open: clr
  Multiplexer #(.enable("false"), .select(5), .width(32)) multiplexer_1 (
    .in0(x0), .in1(ra), .in2(sp), .in3(x3_out), .in4(x4_out), .in5(t0), .in6(t1), .in7(t2), .in8(s0),
    .in9(s1), .in10(a0), .in11(x11_out), .in12(x12_out), .in13(x13_out), .in14(x14_out), .in15(x15_out),
    .in16(x16_out), .in17(x17_out), .in18(x18_out), .in19(x19_out), .in20(x20_out), .in21(x21_out),
    .in22(x22_out), .in23(x23_out), .in24(x24_out), .in25(x25_out), .in26(x26_out), .in27(x27_out),
    .in28(x28_out), .in29(x29_out), .in30(x30_out), .in31(x31_out), .out(Read_Data_1), .sel(rs1));
  Multiplexer #(.enable("false"), .select(5), .width(32)) multiplexer_2 (
    .in0(x0), .in1(ra), .in2(sp), .in3(x3_out), .in4(x4_out), .in5(t0), .in6(t1), .in7(t2), .in8(s0),
    .in9(s1), .in10(a0), .in11(x11_out), .in12(x12_out), .in13(x13_out), .in14(x14_out), .in15(x15_out),
    .in16(x16_out), .in17(x17_out), .in18(x18_out), .in19(x19_out), .in20(x20_out), .in21(x21_out),
    .in22(x22_out), .in23(x23_out), .in24(x24_out), .in25(x25_out), .in26(x26_out), .in27(x27_out),
    .in28(x28_out), .in29(x29_out), .in30(x30_out), .in31(x31_out), .out(Read_Data_2), .sel(rs2));
  Demultiplexer #(.enable("false"), .select(5)) demultiplexer_1 (
    .out1(x1_we), .out2(x2_we), .out3(x3_we), .out4(x4_we), .out5(x5_we), .out6(x6_we), .out7(x7_we),
    .out8(x8_we), .out9(x9_we), .out10(x10_we), .out11(x11_we), .out12(x12_we), .out13(x13_we),
    .out14(x14_we), .out15(x15_we), .out16(x16_we), .out17(x17_we), .out18(x18_we), .out19(x19_we),
    .out20(x20_we), .out21(x21_we), .out22(x22_we), .out23(x23_we), .out24(x24_we), .out25(x25_we),
    .out26(x26_we), .out27(x27_we), .out28(x28_we), .out29(x29_we), .out30(x30_we), .out31(x31_we),
    .in(RegWEn), .sel(rd));  // open: out0

  // Other names for the same wires on the sheet: read_data1[31:0] = Read_Data_1; read_data2[31:0] = Read_Data_2;
  //   read_reg1[4:0] = rs1; read_reg2[4:0] = rs2; write_en = RegWEn; write_reg[4:0] = rd; x0_out[31:0] = x0;
  //   x1_out[31:0] = ra; x2_out[31:0] = sp; x5_out[31:0] = t0; x6_out[31:0] = t1; x7_out[31:0] = t2;
  //   x8_out[31:0] = s0; x9_out[31:0] = s1; x10_out[31:0] = a0

  // Notes on the sheet:
  //   INPUTS to your circuit
  //   DON'T CHANGE THE LOCATIONS OF THE INPUTS AND OUTPUTS!
  //   These are DEBUG/TEST outputs from your circuit.
  //   OUTPUTS from your circuit
endmodule
